# Fritzing sketch project (saved by Fritzing 1.0.4)

parts:
  U1 = ESP 32 DEVKIT DOIT  # not connected
  microSD1 = MicroSD Card Module
  SP1 = SPEAKER [package=pcb_mount_speaker]  # not connected
  Part1 = SparkFun MIDI Shield
  LED1 = LEDs [package=led-1206]
  A1 = Pcm5102A module
  A2 = DORHEA ESP32 GPIO breakout board 30pin
  LED2 = LEDs [package=led-1206]  # not connected
  LED3 = LEDs [package=led-1206]  # not connected
  LED4 = LEDs [package=led-1206]  # not connected
  LED5 = LEDs [package=led-1206]  # not connected
  LED6 = LEDs [package=led-1206]  # not connected
  LED7 = LEDs [package=led-1206]  # not connected
  LED8 = LEDs [package=led-1206]  # not connected
  LED9 = LEDs [package=led-1206]  # not connected
  LED10 = LEDs [package=led-1206]  # not connected
  LED11 = LEDs [package=led-1206]  # not connected
  LED12 = LEDs [package=led-1206]  # not connected
  LED13 = LEDs [package=led-1206]  # not connected
  LED14 = LEDs [package=led-1206]  # not connected
  LED15 = LEDs [package=led-1206]  # not connected
  LED16 = LEDs [package=led-1206]  # not connected

nets:
  GND: microSD1.GND, Part1.GND, LED1.C, A1.Pin_5, A2.Pin_32, A2.Pin_37, A2.Pin_89, A2.Pin_101
  VCC: microSD1.VCC, Part1.3.3V, Part1.VCC, A1.Pin_6, A2.Pin_26, A2.Pin_102, A2.Pin_105, A2.Pin_114
  N1: microSD1.MISO, A2.Pin_122
  N2: microSD1.MOSI, A2.Pin_127
  N3: microSD1.SCK, A2.Pin_121
  N4: microSD1.CS, A2.Pin_120
  N5: Part1.RX-I, A2.Pin_115
  N6: LED1.A, A2.Pin_11
  N7: A1.Pin_2, A2.Pin_9
  N8: A1.Pin_3, A2.Pin_8
  N9: A1.Pin_4, A2.Pin_7

notes:
  There are 126 LEDs in the strip

custom parts:
  Pcm5102A module: Interface I2S PCM5102A DAC Decoder GY-PCM5102 I2S Player Module for Raspberry Pi pHAT Format Board Digital PCM5102 Audio Board.
  DORHEA ESP32 GPIO breakout board 30pin: ESP32 shield 30P expansion board, supports two power supply : DC 6.5-16v and USB 5.V
